# Fritzing sketch greenpithumb (saved by Fritzing 0.9.3b)
breadboards: 1

parts:
  Q1 = MOSFET-NCHANNEL [package=to220v]
  R1 = Resistor [tolerance=±5% resistance=10k package=THT]
  Raspberry_Pi_1 = Raspberry Pi 3 [part_number=RPI-3-V1.2]
  Power_plug1 = Power plug
  IC1 = MCP3008 8-channel 10-bit ADC [part_number=MCP3008]  # not connected
  PART1 = SparkFun Soil Moisture Sensor [part_number=SEN-13322]
  DHT1 = DHT11 Humitidy and Temperature Sensor
  R2 = Resistor [tolerance=±5% resistance=10k package=THT]
  R3 = Photocell (LDR) [package=THT]
  R4 = Resistor [tolerance=±5% resistance=10k package=THT]
  M1 = DC Motor
  R7 = Resistor [tolerance=±5% resistance=56k package=THT]

nets:
  N1: Q1.G, R1.Pin_1, R7.Pin_0
  N2: Q1.D, M1.pin_2
  GND: Q1.S, Raspberry_Pi_1.GND, Power_plug1.GND, PART1.GND, DHT1.GND, R7.Pin_1
  N3: R1.Pin_0, Raspberry_Pi_1.GPIO26
  3V3: Raspberry_Pi_1.3v3, Raspberry_Pi_1.3V3, DHT1.VDD, R2.Pin_0, R3.pin_1
  N4: Raspberry_Pi_1.GPIO21, DHT1.DATA, R2.Pin_1
  N5: Raspberry_Pi_1.GPIO16, PART1.VCC
  N6: Power_plug1.VCC, M1.pin_1
  N7: R3.pin_0, R4.Pin_0

custom parts:
  SparkFun Soil Moisture Sensor: The SparkFun Soil Moisture Sensor is a simple breakout for measuring the moisture in soil and similar materials.
  DHT11 Humitidy and Temperature Sensor: DHT11 Humidity and Temperature Sensor
